# Fritzing sketch sketch (saved by Fritzing 0.9.3b)
breadboards: 1

parts:
  R1 = Resistor [tolerance=±5% resistance=100 package=THT]
  Raspberry_Pi_1 = Raspberry Pi B+
  S2 = Pushbutton [package="[THT]"]
  S3 = Pushbutton [package="[THT]"]
  LED1 = LED - 5mm [color="Green (555nm)" package="5 mm [THT]"]
  LED2 = LED - 5mm [color="Blue (470nm)" package="5 mm [THT]"]
  R2 = Resistor [tolerance=±5% resistance=100 package=THT]

nets:
  N1: R1.Pin_0, Raspberry_Pi_1.GND, S2.Pin_1, S2.Pin_2, S3.Pin_1, S3.Pin_2, R2.Pin_0
  N2: R1.Pin_1, LED1.cathode
  N3: Raspberry_Pi_1.GPIO4, LED1.anode
  N4: Raspberry_Pi_1.GPIO17, S3.Pin_3, S3.Pin_4
  N5: Raspberry_Pi_1.GPIO27, S2.Pin_3, S2.Pin_4
  N6: Raspberry_Pi_1.GPIO22, LED2.anode
  N7: LED2.cathode, R2.Pin_1

notes:
  Button 2
  Button 1
